// Logisim project 2011100019_Kerby_Lovince.circ as structural Verilog
module kerby (
  input  A,
  input  B,
  input  C,
  output S1,
  output S2
);

  wire and_1_out, and_2_out, and_3_out, and_4_out, and_5_out, not_1_out, not_2_out, not_3_out;

  not not_1 (not_1_out, A);
  not not_2 (not_2_out, B);
  not not_3 (not_3_out, C);
  and and_1 (and_1_out, not_1_out, not_2_out, not_3_out);
  and and_2 (and_2_out, B, C);
  or or_1 (S1, and_1_out, and_2_out, and_3_out);
  and and_3 (and_3_out, A, B);
  and and_4 (and_4_out, not_1_out, not_3_out);
  or or_2 (S2, and_4_out, and_5_out);
  and and_5 (and_5_out, not_2_out, not_3_out);
endmodule

module modulo (
  input  J1,
  input  J2,
  input  JO1,
  input  JO2,
  output V1,
  output E,
  output V2
);

  wire and_1_out, and_2_out, and_3_out, and_4_out, and_5_out, and_6_out, and_7_out, and_8_out, and_9_out,
       and_10_out, and_11_out, and_12_out, and_13_out, and_14_out, and_15_out, and_16_out, not_1_out,
       not_2_out, not_3_out, not_4_out;

  not not_1 (not_1_out, J1);
  not not_2 (not_2_out, J2);
  not not_3 (not_3_out, JO1);
  not not_4 (not_4_out, JO2);
  and and_1 (and_1_out, not_2_out, not_4_out);
  and and_2 (and_2_out, not_1_out, JO1);
  and and_3 (and_3_out, not_1_out, J2, JO2);
  and and_4 (and_4_out, J2, JO1);
  and and_5 (and_5_out, J1, not_2_out, not_3_out);
  and and_6 (and_6_out, J1, not_4_out);
  and and_7 (and_7_out, not_1_out, not_2_out);
  and and_8 (and_8_out, not_1_out, not_3_out, not_4_out);
  and and_9 (and_9_out, not_2_out, not_4_out);
  and and_10 (and_10_out, not_1_out, JO1, JO2);
  and and_11 (and_11_out, J1, not_3_out, JO2);
  and and_12 (and_12_out, not_1_out, not_3_out);
  and and_13 (and_13_out, not_1_out, JO2);
  and and_14 (and_14_out, not_3_out, JO2);
  and and_15 (and_15_out, not_1_out, J2);
  and and_16 (and_16_out, J1, not_2_out);
  or or_1 (V1, and_1_out, and_2_out, and_3_out, and_4_out, and_5_out, and_6_out);
  or or_2 (E, and_7_out, and_8_out, and_9_out, and_10_out, and_11_out);
  or or_3 (V2, and_12_out, and_13_out, and_14_out, and_15_out, and_16_out);
endmodule
