// Logisim project Danielpierrelus.circ as structural Verilog: 2 circuits, main circuit main
module main (
  input  A,
  input  B,
  input  C,
  output S,
  output CARGA
);

  wire and_1_out, and_2_out, and_3_out, xor_1_out;

  xor xor_1 (xor_1_out, B, C);
  xor xor_2 (S, xor_1_out, A);
  and and_1 (and_1_out, A, B);
  and and_2 (and_2_out, A, C);
  and and_3 (and_3_out, B, C);
  or or_1 (CARGA, and_1_out, and_2_out, and_3_out);
endmodule

module Somador (
  input  som
);

  wire B_sw1, B_sw2, B_sw3, B_sw4, B_sw5, B_sw6, B_sw7, B_sw8, dipswitch_1_p1, dipswitch_1_p2,
       dipswitch_1_p3, dipswitch_1_p4, dipswitch_1_p5, main1_carga, main1_s, main2_carga, main2_s,
       main3_carga, main3_s, main4_carga, main4_s, main5_carga, main5_s, main6_carga, main6_s, main7_carga,
       main7_s, main8_carga, main8_s, undriven, xor_1_out, xor_2_out, xor_3_out, xor_4_out, xor_5_out,
       xor_6_out, xor_7_out, xor_8_out, xor_9_out;

  // DipSwitch dipswitch_1: pin names not known; wires that end beside it: dipswitch_1_p1, dipswitch_1_p2, dipswitch_1_p3, dipswitch_1_p4, dipswitch_1_p5, dipswitch_1_p2
  DipSwitch B (.sw1(B_sw1), .sw2(B_sw2), .sw3(B_sw3), .sw4(B_sw4), .sw5(B_sw5), .sw6(B_sw6), .sw7(B_sw7), .sw8(B_sw8));
  xor xor_1 (xor_1_out, som, B_sw1);
  xor xor_2 (xor_2_out, som, B_sw2);
  xor xor_3 (xor_3_out, som, B_sw3);
  xor xor_4 (xor_4_out, som, B_sw4);
  xor xor_5 (xor_5_out, som, B_sw5);
  xor xor_6 (xor_6_out, som, B_sw6);
  xor xor_7 (xor_7_out, som, B_sw7);
  xor xor_8 (xor_8_out, som, B_sw8);
  main main1 (.A(som), .B(xor_1_out), .C(dipswitch_1_p3), .S(main1_s), .CARGA(main1_carga));
  main main2 (.A(main1_carga), .B(xor_2_out), .C(dipswitch_1_p4), .S(main2_s), .CARGA(main2_carga));
  main main3 (.A(main2_carga), .B(xor_3_out), .C(dipswitch_1_p1), .S(main3_s), .CARGA(main3_carga));
  main main4 (.A(main3_carga), .B(xor_4_out), .C(dipswitch_1_p1), .S(main4_s), .CARGA(main4_carga));
  main main5 (.A(main4_carga), .B(xor_5_out), .C(dipswitch_1_p2), .S(main5_s), .CARGA(main5_carga));
  main main6 (.A(main5_carga), .B(xor_6_out), .C(undriven), .S(main6_s), .CARGA(main6_carga));
  main main7 (.A(main6_carga), .B(xor_7_out), .C(undriven), .S(main7_s), .CARGA(main7_carga));
  main main8 (.A(main7_carga), .B(xor_8_out), .C(dipswitch_1_p5), .S(main8_s), .CARGA(main8_carga));
  xor xor_9 (xor_9_out, main8_carga, main7_carga);
  LED Overflow (.in(xor_9_out));
  LED a2 (.in(main2_s));
  LED a3 (.in(main3_s));
  LED a4 (.in(main4_s));
  LED a5 (.in(main5_s));
  LED a6 (.in(main6_s));
  LED a7 (.in(main7_s));
  LED B8 (.in(main8_s));
  LED a1 (.in(main1_s));
endmodule
